# Fritzing sketch ColorChangingLight (saved by Fritzing 0.8.7b)
breadboards: 1

parts:
  Part1 = Arduino Uno (Rev3)
  R1 = Resistor [tolerance=±5% resistance=330 package=THT]
  R2 = Resistor [tolerance=±5% resistance=330 package=THT]
  R3 = Resistor [tolerance=±5% resistance=330 package=THT]
  R4 = Resistor [tolerance=±5% resistance=330 package=THT]
  R5 = Resistor [tolerance=±5% resistance=330 package=THT]
  S1 = Pushbutton [package="[THT]"]
  R6 = Resistor [tolerance=±5% resistance=10k package=THT]
  Common_Anode_RGB_LED = RGB LED - (4 legs) [package="5 mm [THT]"]

nets:
  N1: Part1.D9_PWM, R4.Pin_1, R5.Pin_1
  N2: Part1.D10_PWM/SS, R2.Pin_1, R3.Pin_1
  N3: Part1.D11_PWM/MOSI, R1.Pin_1
  N4: Part1.GND, S1.Pin_3, S1.Pin_4
  N5: Part1.D2, S1.Pin_1, S1.Pin_2, R6.Pin_0
  N6: Part1.5V, R6.Pin_1, Common_Anode_RGB_LED.common_anode
  N7: R1.Pin_0, Common_Anode_RGB_LED.red_cathode
  N8: R2.Pin_0, R3.Pin_0, Common_Anode_RGB_LED.green_cathode
  N9: R4.Pin_0, R5.Pin_0, Common_Anode_RGB_LED.blue_cathode
