# Fritzing sketch TrafficLightsButton (saved by Fritzing 0.8.7b)
breadboards: 1

parts:
  Single-board_microcontroller = Arduino Uno (Rev3)
  LED1 = LED - 5mm [color="Red (633nm)" package="5 mm [THT]"]
  R1 = Resistor [tolerance=±5% resistance=220 package=THT]
  LED2 = LED - 5mm [color="Yellow (585nm)" package="5 mm [THT]"]
  R2 = Resistor [tolerance=±5% resistance=220 package=THT]
  LED3 = LED - 5mm [color="Green (555nm)" package="5 mm [THT]"]
  R3 = Resistor [tolerance=±5% resistance=220 package=THT]
  LED4 = LED - 5mm [color="Red (633nm)" package="5 mm [THT]"]
  R4 = Resistor [tolerance=±5% resistance=220 package=THT]
  LED5 = LED - 5mm [color="Green (555nm)" package="5 mm [THT]"]
  R5 = Resistor [tolerance=±5% resistance=220 package=THT]
  S1 = Pushbutton [package="[THT]"]
  R6 = Resistor [tolerance=±5% resistance=10k package=THT]

nets:
  N1: Single-board_microcontroller.D8, R2.Pin_1
  N2: Single-board_microcontroller.D12/MISO, R1.Pin_1
  N3: Single-board_microcontroller.GND, LED1.cathode, LED2.cathode, LED3.cathode, LED4.cathode, LED5.cathode, S1.Pin_3, S1.Pin_4
  N4: Single-board_microcontroller.D2, R5.Pin_1
  N5: Single-board_microcontroller.D4, R4.Pin_1
  N6: Single-board_microcontroller.D5_PWM, S1.Pin_1, S1.Pin_2, R6.Pin_0
  N7: Single-board_microcontroller.D7, R3.Pin_1
  N8: Single-board_microcontroller.5V, R6.Pin_1
  N9: LED1.anode, R1.Pin_0
  N10: LED2.anode, R2.Pin_0
  N11: LED3.anode, R3.Pin_0
  N12: LED4.anode, R4.Pin_0
  N13: LED5.anode, R5.Pin_0
